// Logisim project 4.1UniversalGates.circ as structural Verilog: 1 circuit, main circuit main
module main (
  input  Z,
  input  X,
  input  Y,
  input  W,
  output out_5
);

  wire nand_1_out, nand_2_out, nand_3_out;

  nand nand_1 (nand_1_out, X, X, Y);
  nand nand_2 (nand_2_out, Z, nand_1_out);
  nand nand_3 (nand_3_out, nand_1_out, W);
  nand nand_4 (out_5, nand_2_out, nand_3_out);
endmodule
