// Logisim project 4.2ParityCounter.circ as structural Verilog: 1 circuit, main circuit main
module main (
  input  A,
  input  B,
  input  C,
  input  D,
  output F1,
  output F2,
  output F0
);

  wire and_1_out, and_2_out, and_3_out, and_4_out, and_6_out, and_7_out, and_8_out, and_9_out, and_10_out,
       and_11_out, and_12_out, and_13_out, and_14_out, and_15_out, not_1_out, not_2_out, not_3_out,
       not_4_out, or_1_out, or_2_out, or_4_out, or_5_out;

  not not_1 (not_1_out, A);
  not not_2 (not_2_out, B);
  not not_3 (not_3_out, C);
  not not_4 (not_4_out, D);
  and and_1 (and_1_out, not_2_out, C, D);
  and and_2 (and_2_out, B, not_3_out, D);
  and and_3 (and_3_out, B, C, not_4_out);
  and and_4 (and_4_out, not_1_out, B, C, D);
  and and_5 (F2, A, B, C, D);
  and and_6 (and_6_out, not_3_out, A, not_2_out, D);
  and and_7 (and_7_out, A, C, not_2_out, not_4_out);
  and and_8 (and_8_out, A, B, not_3_out, not_4_out);
  and and_9 (and_9_out, not_1_out, not_2_out, not_3_out, D);
  and and_10 (and_10_out, not_1_out, not_2_out, C, not_4_out);
  and and_11 (and_11_out, not_1_out, B, not_3_out, not_4_out);
  and and_12 (and_12_out, A, not_2_out, not_3_out, not_4_out);
  and and_13 (and_13_out, A, not_2_out, C, D);
  and and_14 (and_14_out, A, B, not_3_out, D);
  and and_15 (and_15_out, A, B, C, not_4_out);
  or or_1 (or_1_out, and_1_out, and_2_out, and_3_out);
  or or_2 (or_2_out, and_4_out, and_6_out, and_7_out, and_8_out);
  or or_3 (F1, or_1_out, or_2_out);
  or or_4 (or_4_out, and_4_out, and_9_out, and_10_out, and_11_out);
  or or_5 (or_5_out, and_12_out, and_13_out, and_14_out, and_15_out);
  or or_6 (F0, or_4_out, or_5_out);
endmodule
