// Logisim project 4.3adders.circ as structural Verilog: 1 circuit, main circuit main
module main (
  input  A6,
  input  A0,
  input  A1,
  input  A2,
  input  A3,
  input  A4,
  input  A5,
  output F0,
  output F1,
  output F2
);

  wire adder_1_cout, adder_1_out, adder_2_cout, adder_2_out, adder_3_cout;

  Adder #(.width(1)) adder_1 (.a(A1), .b(A2), .out(adder_1_out), .cin(A0), .cout(adder_1_cout));
  Adder #(.width(1)) adder_2 (.a(A4), .b(A5), .out(adder_2_out), .cin(A3), .cout(adder_2_cout));
  Adder #(.width(1)) adder_3 (.a(adder_1_out), .b(adder_2_out), .out(F0), .cin(A6), .cout(adder_3_cout));
  Adder #(.width(1)) adder_4 (.a(adder_1_cout), .b(adder_2_cout), .out(F1), .cin(adder_3_cout), .cout(F2));

  // Notes on the sheet:
  //   S1
  //   C1
  //   S2
  //   C2
  //   C3
endmodule
